// Logisim project 4bitComparator.circ as structural Verilog: 2 circuits, main circuit main
module main (
  input  [3:0] A,
  input  [3:0] B
);

  wire [2:0] SEL;
  wire [3:0] binary_to_bcd_converter_1_p2, binary_to_bcd_converter_1_p3, binary_to_bcd_converter_2_p2,
       binary_to_bcd_converter_2_p3;
  wire [34:0] multiplexer_1_out;

  comparator4bit comparator4bit_1 (.A_B(SEL[2]), .A_B_2(SEL[1]), .A_B_3(SEL[0]), .in_1(A), .in_2(B));
  // Probe on SEL[2]
  // Probe on SEL[1]
  // Probe on SEL[0]
  // Binary_to_BCD_converter #(.binvalue(4)) binary_to_bcd_converter_1: pin names not known; wires that end beside it: A, binary_to_bcd_converter_1_p2, binary_to_bcd_converter_1_p3
  Multiplexer #(.select(3), .width(35)) multiplexer_1 (
    .in1(35'h1051100), .in2(35'h2850a00), .in4(35'h4450400), .out(multiplexer_1_out), .sel(SEL));  // open: in0, in3, in5, in6, in7
  Hex_Digit_Display hex_digit_display_1 (.value(binary_to_bcd_converter_1_p2));  // open: dp
  Hex_Digit_Display hex_digit_display_2 (.value(binary_to_bcd_converter_1_p3));  // open: dp
  DotMatrix dotmatrix_1 (
    .col0(multiplexer_1_out[34:28]), .col1(multiplexer_1_out[27:21]), .col2(multiplexer_1_out[20:14]),
    .col3(multiplexer_1_out[13:7]), .col4(multiplexer_1_out[6:0]));
  Hex_Digit_Display hex_digit_display_3 (.value(binary_to_bcd_converter_2_p2));  // open: dp
  Hex_Digit_Display hex_digit_display_4 (.value(binary_to_bcd_converter_2_p3));  // open: dp
  // Binary_to_BCD_converter #(.binvalue(4)) binary_to_bcd_converter_2: pin names not known; wires that end beside it: B, binary_to_bcd_converter_2_p2, binary_to_bcd_converter_2_p3

  // Notes on the sheet:
  //   A
  //   B
endmodule

module comparator4bit (
  input  [3:0] in_1,
  input  [3:0] in_2,
  output A_B,
  output A_B_2,
  output A_B_3
);

  wire EQ0, EQ1, EQ2, EQ3, GR0, GR1, GR2, GR3, not_1_out, not_2_out, not_3_out, not_4_out;

  not not_1 (not_1_out, in_2[3]);
  not not_2 (not_2_out, in_2[2]);
  not not_3 (not_3_out, in_2[1]);
  not not_4 (not_4_out, in_2[0]);
  and and_1 (GR3, in_1[3], not_1_out);
  and and_2 (GR2, EQ3, in_1[2], not_2_out);
  and and_3 (GR1, EQ3, EQ2, in_1[1], not_3_out);
  and and_4 (GR0, EQ3, EQ2, EQ1, in_1[0], not_4_out);
  xnor xnor_1 (EQ3, in_1[3], in_2[3]);
  xnor xnor_2 (EQ2, in_1[2], in_2[2]);
  xnor xnor_3 (EQ1, in_1[1], in_2[1]);
  xnor xnor_4 (EQ0, in_1[0], in_2[0]);
  or or_1 (A_B, GR0, GR1, GR2, GR3);
  and and_5 (A_B_2, EQ0, EQ1, EQ2, EQ3);
  nor nor_1 (A_B_3, A_B, A_B_2);

  // Other names for the same wires on the sheet: EQ = A_B_2; GR = A_B; A0 = in_1[0]; A1 = in_1[1]; A2 = in_1[2];
  //   A3 = in_1[3]; B0 = in_2[0]; B1 = in_2[1]; B2 = in_2[2]; B3 = in_2[3]; LE = A_B_3

  // Notes on the sheet:
  //   A
  //   B
endmodule
