// Logisim project 4bitDecoder.circ as structural Verilog: 3 circuits, main circuit main
module main (
  input  [3:0] in_1,
  input  in_2
);

  wire decoder4bit_1__0, decoder4bit_1__1, decoder4bit_1__2, decoder4bit_1__3, decoder4bit_1__4,
       decoder4bit_1__5, decoder4bit_1__6, decoder4bit_1__7, decoder4bit_1__8, decoder4bit_1__9,
       decoder4bit_1__10, decoder4bit_1__11, decoder4bit_1__12, decoder4bit_1__13, decoder4bit_1__14,
       decoder4bit_1__15, decoder_1_out0, decoder_1_out1, decoder_1_out2, decoder_1_out3, decoder_1_out4,
       decoder_1_out5, decoder_1_out6, decoder_1_out7, decoder_1_out8, decoder_1_out9, decoder_1_out10,
       decoder_1_out11, decoder_1_out12, decoder_1_out13, decoder_1_out14, decoder_1_out15;

  Decoder #(.select(4)) decoder_1 (
    .out0(decoder_1_out0), .out1(decoder_1_out1), .out2(decoder_1_out2), .out3(decoder_1_out3),
    .out4(decoder_1_out4), .out5(decoder_1_out5), .out6(decoder_1_out6), .out7(decoder_1_out7),
    .out8(decoder_1_out8), .out9(decoder_1_out9), .out10(decoder_1_out10), .out11(decoder_1_out11),
    .out12(decoder_1_out12), .out13(decoder_1_out13), .out14(decoder_1_out14), .out15(decoder_1_out15),
    .sel(in_1), .en(in_2));
  decoder4bit decoder4bit_1 (
    ._15(decoder4bit_1__15), ._0(decoder4bit_1__0), ._1(decoder4bit_1__1), ._2(decoder4bit_1__2),
    ._3(decoder4bit_1__3), ._4(decoder4bit_1__4), ._5(decoder4bit_1__5), ._6(decoder4bit_1__6),
    ._7(decoder4bit_1__7), ._8(decoder4bit_1__8), ._9(decoder4bit_1__9), ._10(decoder4bit_1__10),
    ._11(decoder4bit_1__11), ._12(decoder4bit_1__12), ._13(decoder4bit_1__13), ._14(decoder4bit_1__14),
    .in_2(in_1), .ENABLE(in_2));
  LED led_1 (.in(decoder_1_out0));
  LED led_2 (.in(decoder_1_out1));
  LED led_3 (.in(decoder_1_out2));
  LED led_4 (.in(decoder_1_out3));
  LED led_5 (.in(decoder_1_out4));
  LED led_6 (.in(decoder_1_out5));
  LED led_7 (.in(decoder_1_out6));
  LED led_8 (.in(decoder_1_out7));
  LED led_9 (.in(decoder_1_out8));
  LED led_10 (.in(decoder_1_out9));
  LED led_11 (.in(decoder_1_out10));
  LED led_12 (.in(decoder_1_out11));
  LED led_13 (.in(decoder_1_out12));
  LED led_14 (.in(decoder_1_out13));
  LED led_15 (.in(decoder_1_out14));
  LED led_16 (.in(decoder_1_out15));
  LED led_17 (.in(decoder4bit_1__0));
  LED led_18 (.in(decoder4bit_1__1));
  LED led_19 (.in(decoder4bit_1__2));
  LED led_20 (.in(decoder4bit_1__3));
  LED led_21 (.in(decoder4bit_1__4));
  LED led_22 (.in(decoder4bit_1__5));
  LED led_23 (.in(decoder4bit_1__6));
  LED led_24 (.in(decoder4bit_1__7));
  LED led_25 (.in(decoder4bit_1__8));
  LED led_26 (.in(decoder4bit_1__9));
  LED led_27 (.in(decoder4bit_1__10));
  LED led_28 (.in(decoder4bit_1__11));
  LED led_29 (.in(decoder4bit_1__12));
  LED led_30 (.in(decoder4bit_1__13));
  LED led_31 (.in(decoder4bit_1__14));
  LED led_32 (.in(decoder4bit_1__15));

  // Notes on the sheet:
  //   SELECT
  //   ENABLE
  //   0
  //   1
  //   2
  //   3
  //   4
  //   5
  //   6
  //   7
  //   8
  //   9
  //   10
  //   11
  //   12
  //   13
  //   14
  //   15
endmodule

module decoder4bit (
  input  ENABLE,
  input  [3:0] in_2,
  output _0,
  output _1,
  output _2,
  output _3,
  output _4,
  output _5,
  output _6,
  output _7,
  output _8,
  output _9,
  output _10,
  output _11,
  output _12,
  output _13,
  output _14,
  output _15
);

  wire not_1_out, not_2_out, not_3_out, not_4_out;

  not not_1 (not_1_out, in_2[0]);
  not not_2 (not_2_out, in_2[1]);
  not not_3 (not_3_out, in_2[2]);
  not not_4 (not_4_out, in_2[3]);
  and and_1 (_0, not_1_out, not_2_out, ENABLE, not_3_out, not_4_out);
  and and_2 (_1, not_2_out, not_3_out, ENABLE, not_4_out, in_2[0]);
  and and_3 (_2, not_4_out, not_3_out, ENABLE, in_2[1], not_1_out);
  and and_4 (_3, in_2[0], in_2[1], ENABLE, not_3_out, not_4_out);
  and and_5 (_4, in_2[2], not_1_out, ENABLE, not_2_out, not_4_out);
  and and_6 (_5, in_2[0], in_2[2], ENABLE, not_2_out, not_4_out);
  and and_7 (_6, in_2[1], in_2[2], ENABLE, not_1_out, not_4_out);
  and and_8 (_7, in_2[0], in_2[1], ENABLE, in_2[2], not_4_out);
  and and_9 (_8, in_2[3], not_1_out, ENABLE, not_2_out, not_3_out);
  and and_10 (_9, in_2[0], in_2[3], ENABLE, not_2_out, not_3_out);
  and and_11 (_10, in_2[1], in_2[3], ENABLE, not_1_out, not_3_out);
  and and_12 (_11, in_2[0], in_2[1], ENABLE, in_2[3], not_3_out);
  and and_13 (_12, in_2[2], in_2[3], ENABLE, not_1_out, not_2_out);
  and and_14 (_13, in_2[0], in_2[2], ENABLE, in_2[3], not_2_out);
  and and_15 (_14, in_2[1], in_2[2], ENABLE, in_2[3], not_1_out);
  and and_16 (_15, in_2[0], in_2[1], ENABLE, in_2[2], in_2[3]);

  // Notes on the sheet:
  //   SELECT
  //   A
  //   B
  //   C
  //   D
  //   A'
  //   B'
  //   C'
  //   D'
endmodule

module decoder1bit (
  input  EN,
  input  SEL,
  output _0,
  output _1
);

  wire not_1_out;

  not not_1 (not_1_out, SEL);
  and and_1 (_0, not_1_out, EN);
  and and_2 (_1, SEL, EN);
endmodule
