// Logisim project 4bitFullAdder.circ as structural Verilog: 3 circuits, main circuit main
module main (
  input  in_1,
  input  [3:0] A,
  input  [3:0] B,
  input  in_4
);

  wire [3:0] adder_1_out, binary_to_bcd_converter_1_p2, binary_to_bcd_converter_1_p3,
       binary_to_bcd_converter_2_p2, binary_to_bcd_converter_2_p3, fulladder4bit_1_out_4;
  wire [4:4] adder_1_cout, fulladder4bit_1_out_5;

  fullAdder4bit fulladder4bit_1 (
    .out_5(fulladder4bit_1_out_5[4]), .out_4(fulladder4bit_1_out_4), .in_2(A), .in_3(B), .in_1(in_1));
  Adder #(.width(4)) adder_1 (.a(A), .b(B), .out(adder_1_out), .cin(in_4), .cout(adder_1_cout[4]));
  Hex_Digit_Display hex_digit_display_1 (.value(binary_to_bcd_converter_1_p2));  // open: dp
  // Binary_to_BCD_converter #(.binvalue(5)) binary_to_bcd_converter_1: pin names not known; wires that end beside it: {fulladder4bit_1_out_5[4], fulladder4bit_1_out_4}, binary_to_bcd_converter_1_p2, binary_to_bcd_converter_1_p3
  Hex_Digit_Display hex_digit_display_2 (.value(binary_to_bcd_converter_2_p2));  // open: dp
  // Binary_to_BCD_converter #(.binvalue(5)) binary_to_bcd_converter_2: pin names not known; wires that end beside it: {adder_1_cout[4], adder_1_out}, binary_to_bcd_converter_2_p2, binary_to_bcd_converter_2_p3
  Hex_Digit_Display hex_digit_display_3 (.value(binary_to_bcd_converter_1_p3));  // open: dp
  Hex_Digit_Display hex_digit_display_4 (.value(binary_to_bcd_converter_2_p3));  // open: dp
endmodule

module fullAdder4bit (
  input  in_1,
  input  [3:0] in_2,
  input  [3:0] in_3,
  output [3:0] out_4,
  output out_5
);

  wire fulladder1bit_1_cout, fulladder1bit_2_cout, fulladder1bit_3_cout;

  fullAdder1bit fulladder1bit_1 (.Sum(out_4[0]), .Cout(fulladder1bit_1_cout), .A(in_2[0]), .B(in_3[0]), .Cin(in_1));
  fullAdder1bit fulladder1bit_2 (
    .Sum(out_4[1]), .Cout(fulladder1bit_2_cout), .A(in_2[1]), .B(in_3[1]), .Cin(fulladder1bit_1_cout));
  fullAdder1bit fulladder1bit_3 (
    .Sum(out_4[2]), .Cout(fulladder1bit_3_cout), .A(in_2[2]), .B(in_3[2]), .Cin(fulladder1bit_2_cout));
  fullAdder1bit fulladder1bit_4 (.Sum(out_4[3]), .Cout(out_5), .A(in_2[3]), .B(in_3[3]), .Cin(fulladder1bit_3_cout));

  // Other names for the same wires on the sheet: A0 = in_2[0]; A1 = in_2[1]; A2 = in_2[2]; A3 = in_2[3]; B0 = in_3[0];
  //   B1 = in_3[1]; B2 = in_3[2]; B3 = in_3[3]
endmodule

module fullAdder1bit (
  input  A,
  input  B,
  input  Cin,
  output Sum,
  output Cout
);

  wire and_1_out, and_2_out, xor_1_out;

  xor xor_1 (xor_1_out, A, B);
  xor xor_2 (Sum, xor_1_out, Cin);
  and and_1 (and_1_out, xor_1_out, Cin);
  and and_2 (and_2_out, A, B);
  or or_1 (Cout, and_1_out, and_2_out);
endmodule
