// Logisim project 4bitFullSubtractor.circ as structural Verilog: 3 circuits, main circuit main
module main (
  input  in_1,
  input  [3:0] A,
  input  [3:0] B,
  input  in_4
);

  wire [3:0] binary_to_bcd_converter_1_p2, binary_to_bcd_converter_1_p3, binary_to_bcd_converter_2_p2,
       binary_to_bcd_converter_2_p3, fullsubtracter4bit_1_out_4, subtractor_1_out;
  wire [4:4] fullsubtracter4bit_1_out_5, subtractor_1_bout;

  fullSubtracter4bit fullsubtracter4bit_1 (
    .out_5(fullsubtracter4bit_1_out_5[4]), .out_4(fullsubtracter4bit_1_out_4), .in_2(A), .in_3(B), .in_1(in_1));
  Subtractor #(.width(4)) subtractor_1 (.a(A), .b(B), .out(subtractor_1_out), .bin(in_4), .bout(subtractor_1_bout[4]));
  Hex_Digit_Display hex_digit_display_1 (.value(binary_to_bcd_converter_1_p2));  // open: dp
  // Binary_to_BCD_converter #(.binvalue(5)) binary_to_bcd_converter_1: pin names not known; wires that end beside it: {fullsubtracter4bit_1_out_5[4], fullsubtracter4bit_1_out_4}, binary_to_bcd_converter_1_p2, binary_to_bcd_converter_1_p3
  Hex_Digit_Display hex_digit_display_2 (.value(binary_to_bcd_converter_2_p2));  // open: dp
  // Binary_to_BCD_converter #(.binvalue(5)) binary_to_bcd_converter_2: pin names not known; wires that end beside it: {subtractor_1_bout[4], subtractor_1_out}, binary_to_bcd_converter_2_p2, binary_to_bcd_converter_2_p3
  Hex_Digit_Display hex_digit_display_3 (.value(binary_to_bcd_converter_1_p3));  // open: dp
  Hex_Digit_Display hex_digit_display_4 (.value(binary_to_bcd_converter_2_p3));  // open: dp
endmodule

module fullSubtracter4bit (
  input  in_1,
  input  [3:0] in_2,
  input  [3:0] in_3,
  output [3:0] out_4,
  output out_5
);

  wire fullsubtracter1bit_1_bout, fullsubtracter1bit_2_bout, fullsubtracter1bit_3_bout;

  fullSubtracter1bit fullsubtracter1bit_1 (
    .Diff(out_4[0]), .Bout(fullsubtracter1bit_1_bout), .B(in_3[0]), .Bin(in_1), .A(in_2[0]));
  fullSubtracter1bit fullsubtracter1bit_2 (
    .Diff(out_4[1]), .Bout(fullsubtracter1bit_2_bout), .B(in_3[1]), .Bin(fullsubtracter1bit_1_bout),
    .A(in_2[1]));
  fullSubtracter1bit fullsubtracter1bit_3 (
    .Diff(out_4[2]), .Bout(fullsubtracter1bit_3_bout), .B(in_3[2]), .Bin(fullsubtracter1bit_2_bout),
    .A(in_2[2]));
  fullSubtracter1bit fullsubtracter1bit_4 (
    .Diff(out_4[3]), .Bout(out_5), .B(in_3[3]), .Bin(fullsubtracter1bit_3_bout), .A(in_2[3]));

  // Other names for the same wires on the sheet: A0 = in_2[0]; A1 = in_2[1]; A2 = in_2[2]; A3 = in_2[3]; B0 = in_3[0];
  //   B1 = in_3[1]; B2 = in_3[2]; B3 = in_3[3]
endmodule

module fullSubtracter1bit (
  input  A,
  input  B,
  input  Bin,
  output Diff,
  output Bout
);

  wire and_1_out, and_2_out, and_3_out, not_1_out, xor_1_out;

  xor xor_1 (xor_1_out, A, B);
  not not_1 (not_1_out, A);
  xor xor_2 (Diff, xor_1_out, Bin);
  and and_1 (and_1_out, not_1_out, B);
  and and_2 (and_2_out, B, Bin);
  and and_3 (and_3_out, not_1_out, Bin);
  or or_1 (Bout, and_1_out, and_2_out, and_3_out);
endmodule
