// Logisim project 4bitUpDownCounter.circ as structural Verilog: 2 circuits, main circuit main
module main (
  input  ResetUp,
  input  ClockUp,
  input  Hard_Set_FF,
  input  J_FF,
  input  K_FF,
  input  Clock_FF,
  input  Hard_Reset_FF,
  input  EnOscUp,
  input  ClrOscUp,
  input  ResetDown,
  input  UpDown,
  input  ClockDown,
  input  ResetUpDown,
  input  ClockUpDown,
  input  EnOscUpDown,
  input  EnOscDown,
  input  ClrOscUpDown,
  input  ClrOscDown,
  input  Up_Down,
  input  Reset,
  input  Clock
);

  wire and_1_out, and_2_out, and_3_out, and_4_out, and_5_out, and_6_out, B0, B1, B2, B3, D0, D1, D2, D3,
       j_k_ff_3_q, j_k_ff_3_qn, j_k_ff_6_qn, j_k_ff_7_qn, j_k_ff_8_qn, j_k_ff_9_qn, j_k_ff_10_qn,
       j_k_ff_11_qn, not_1_out, or_1_out, or_2_out, or_3_out, U0, U1, U2, U3;
  wire [3:0] counter_1_q, updowncounter4bit_1_out_4;

  // Digital_Oscilloscope #(.nState(17)) DownOscilloscope: pin names not known; wires that end beside it: ClockDown, D0, D1, D2, D3, EnOscDown, ClrOscDown, D0
  J_K_Flip_Flop j_k_ff_1 (.J(1'b1), .K(1'b1), .clk(ClockDown), .Qn(D0), .reset(ResetDown));  // open: Q, preset
  J_K_Flip_Flop j_k_ff_2 (.J(1'b1), .K(1'b1), .clk(D0), .Qn(D1), .reset(ResetDown));  // open: Q, preset
  J_K_Flip_Flop j_k_ff_3 (
    .J(J_FF), .K(K_FF), .clk(Clock_FF), .Q(j_k_ff_3_q), .Qn(j_k_ff_3_qn), .preset(Hard_Set_FF),
    .reset(Hard_Reset_FF));
  // Probe on j_k_ff_3_q
  // Probe on j_k_ff_3_qn
  J_K_Flip_Flop j_k_ff_4 (.J(1'b1), .K(1'b1), .clk(D1), .Qn(D2), .reset(ResetDown));  // open: Q, preset
  J_K_Flip_Flop j_k_ff_5 (.J(1'b1), .K(1'b1), .clk(D2), .Qn(D3), .reset(ResetDown));  // open: Q, preset
  // Probe on {D3, D2, D1, D0}
  Counter #(.max('hf), .width(4)) counter_1 (
    .clr(Reset), .up(Up_Down), .clk(Clock), .Q(counter_1_q));  // open: load, count, D, carry
  // Probe on updowncounter4bit_1_out_4
  upDownCounter4bit updowncounter4bit_1 (.out_4(updowncounter4bit_1_out_4), .in_1(Up_Down), .in_2(Reset), .in_3(Clock));
  J_K_Flip_Flop j_k_ff_6 (
    .J(1'b1), .K(1'b1), .clk(ClockUpDown), .Q(B0), .Qn(j_k_ff_6_qn), .reset(ResetUpDown));  // open: preset
  not not_1 (not_1_out, UpDown);
  // Probe on counter_1_q
  and and_1 (and_1_out, UpDown, B0);
  and and_2 (and_2_out, j_k_ff_6_qn, not_1_out);
  J_K_Flip_Flop j_k_ff_7 (
    .J(1'b1), .K(1'b1), .clk(ClockUp), .Q(U0), .Qn(j_k_ff_7_qn), .reset(ResetUp));  // open: preset
  // Digital_Oscilloscope #(.nState(17)) UpOscilloscope: pin names not known; wires that end beside it: ClockUp, U0, U1, U2, U3, EnOscUp, ClrOscUp
  J_K_Flip_Flop j_k_ff_8 (
    .J(or_1_out), .K(or_1_out), .clk(ClockUpDown), .Q(B1), .Qn(j_k_ff_8_qn), .reset(ResetUpDown));  // open: preset
  or or_1 (or_1_out, and_1_out, and_2_out);
  // Digital_Oscilloscope #(.nState(17)) UpDownOscilloscope: pin names not known; wires that end beside it: ClockUpDown, B0, B1, B2, B3, EnOscUpDown, ClrOscUpDown
  J_K_Flip_Flop j_k_ff_9 (
    .J(1'b1), .K(1'b1), .clk(j_k_ff_7_qn), .Q(U1), .Qn(j_k_ff_9_qn), .reset(ResetUp));  // open: preset
  and and_3 (and_3_out, and_1_out, B1);
  or or_2 (or_2_out, and_3_out, and_4_out);
  and and_4 (and_4_out, j_k_ff_8_qn, and_2_out);
  J_K_Flip_Flop j_k_ff_10 (
    .J(1'b1), .K(1'b1), .clk(j_k_ff_9_qn), .Q(U2), .Qn(j_k_ff_10_qn), .reset(ResetUp));  // open: preset
  J_K_Flip_Flop j_k_ff_11 (
    .J(or_2_out), .K(or_2_out), .clk(ClockUpDown), .Q(B2), .Qn(j_k_ff_11_qn), .reset(ResetUpDown));  // open: preset
  J_K_Flip_Flop j_k_ff_12 (.J(1'b1), .K(1'b1), .clk(j_k_ff_10_qn), .Q(U3), .reset(ResetUp));  // open: Qn, preset
  and and_5 (and_5_out, and_3_out, B2);
  and and_6 (and_6_out, j_k_ff_11_qn, and_4_out);
  // Probe on {B3, B2, B1, B0}
  J_K_Flip_Flop j_k_ff_13 (
    .J(or_3_out), .K(or_3_out), .clk(ClockUpDown), .Q(B3), .reset(ResetUpDown));  // open: Qn, preset
  or or_3 (or_3_out, and_5_out, and_6_out);
  // Probe on {U3, U2, U1, U0}

  // Other names for the same wires on the sheet: CLKD = ClockDown; CLKU = ClockUp; CLKUD = ClockUpDown;
  //   DR = ResetDown; RST = ResetUpDown; UR = ResetUp

  // Notes on the sheet:
  //   J = 0 : K = 0 ----- Unchanged Q = Q
  //   J = 1 : K = 0 ----- Set Output Q = 1
  //   J = 0 : K = 1 ----- Reset Output Q = 0
  //   J = 1 : K = 1 ----- Toggle Output Q = Q'
endmodule

module upDownCounter4bit (
  input  in_1,
  input  in_2,
  input  in_3,
  output [3:0] out_4
);

  wire and_1_out, and_2_out, and_3_out, and_4_out, and_5_out, and_6_out, j_k_ff_1_qn, j_k_ff_2_qn,
       j_k_ff_3_qn, not_1_out, or_1_out, or_2_out, or_3_out;

  J_K_Flip_Flop j_k_ff_1 (
    .J(1'b1), .K(1'b1), .clk(in_3), .Q(out_4[0]), .Qn(j_k_ff_1_qn), .reset(in_2));  // open: preset
  not not_1 (not_1_out, in_1);
  and and_1 (and_1_out, in_1, out_4[0]);
  and and_2 (and_2_out, j_k_ff_1_qn, not_1_out);
  J_K_Flip_Flop j_k_ff_2 (
    .J(or_1_out), .K(or_1_out), .clk(in_3), .Q(out_4[1]), .Qn(j_k_ff_2_qn), .reset(in_2));  // open: preset
  or or_1 (or_1_out, and_1_out, and_2_out);
  and and_3 (and_3_out, and_1_out, out_4[1]);
  or or_2 (or_2_out, and_3_out, and_4_out);
  and and_4 (and_4_out, j_k_ff_2_qn, and_2_out);
  J_K_Flip_Flop j_k_ff_3 (
    .J(or_2_out), .K(or_2_out), .clk(in_3), .Q(out_4[2]), .Qn(j_k_ff_3_qn), .reset(in_2));  // open: preset
  and and_5 (and_5_out, and_3_out, out_4[2]);
  and and_6 (and_6_out, j_k_ff_3_qn, and_4_out);
  J_K_Flip_Flop j_k_ff_4 (.J(or_3_out), .K(or_3_out), .clk(in_3), .Q(out_4[3]), .reset(in_2));  // open: Qn, preset
  or or_3 (or_3_out, and_5_out, and_6_out);

  // Other names for the same wires on the sheet: CLKUD = in_3; B0 = out_4[0]; B1 = out_4[1]; B2 = out_4[2];
  //   B3 = out_4[3]; RST = in_2
endmodule
