// Logisim project 7SegmentDisplayUsage.circ as structural Verilog: 1 circuit, main circuit main
module main (
  input  in_1,
  input  in_2,
  input  in_3,
  input  in_4,
  input  in_5,
  input  in_6,
  input  [3:0] in_7,
  input  [12:0] in_8,
  input  in_9,
  input  in_10,
  input  [3:0] in_11,
  input  in_12,
  input  in_13,
  input  in_14,
  input  in_15,
  input  in_16,
  input  in_17,
  input  in_18,
  input  in_19,
  input  [3:0] in_20,
  input  in_21,
  input  in_22,
  input  [3:0] Digit,
  input  in_24,
  input  [12:0] in_25,
  input  [3:0] in_26
);

  wire SE_A, SE_B, SE_C, SE_D, SE_E, SE_F, SE_G;
  wire [3:0] binary_to_bcd_converter_1_p2, binary_to_bcd_converter_1_p3, binary_to_bcd_converter_1_p4,
       binary_to_bcd_converter_1_p5, binary_to_bcd_converter_2_p2, binary_to_bcd_converter_2_p3,
       binary_to_bcd_converter_2_p4, binary_to_bcd_converter_2_p5;

  _7_Segment_Display u_7_segment_display_1 (
    .g(in_21), .f(in_19), .a(in_13), .b(in_14), .e(in_17), .d(in_16), .c(in_15), .dp(in_22));
  _7_Segment_Display u_7_segment_display_2 ();  // open: g, f, a, b, e, d, c, dp
  // BCD_to_7_Segment_decoder bcd_to_7_segment_decoder_1: pin names not known; wires that end beside it: in_26
  _7_Segment_Display u_7_segment_display_3 ();  // open: g, f, a, b, e, d, c, dp
  // BCD_to_7_Segment_decoder bcd_to_7_segment_decoder_2: pin names not known
  _7_Segment_Display u_7_segment_display_4 (
    .g(in_10), .f(in_9), .a(in_1), .b(in_2), .e(in_5), .d(in_4), .c(in_3), .dp(in_12));
  Hex_Digit_Display hex_digit_display_1 (.value(in_7));  // open: dp
  Hex_Digit_Display hex_digit_display_2 (.value(binary_to_bcd_converter_1_p2));  // open: dp
  // Binary_to_BCD_converter #(.binvalue(13)) binary_to_bcd_converter_1: pin names not known; wires that end beside it: in_25, binary_to_bcd_converter_1_p2, binary_to_bcd_converter_1_p3, binary_to_bcd_converter_1_p4, binary_to_bcd_converter_1_p5
  _7_Segment_Display u_7_segment_display_5 ();  // open: g, f, a, b, e, d, c, dp
  // BCD_to_7_Segment_decoder bcd_to_7_segment_decoder_3: pin names not known; wires that end beside it: in_6, in_11
  Hex_Digit_Display hex_digit_display_3 (.value(in_20));  // open: dp
  Hex_Digit_Display hex_digit_display_4 (.value(binary_to_bcd_converter_1_p3));  // open: dp
  Hex_Digit_Display hex_digit_display_5 (.value(binary_to_bcd_converter_1_p4));  // open: dp
  Hex_Digit_Display hex_digit_display_6 (.value(binary_to_bcd_converter_1_p5));  // open: dp
  Hex_Digit_Display hex_digit_display_7 (.value(binary_to_bcd_converter_2_p2));  // open: dp
  // Binary_to_BCD_converter #(.binvalue(13)) binary_to_bcd_converter_2: pin names not known; wires that end beside it: in_8, binary_to_bcd_converter_2_p2, binary_to_bcd_converter_2_p3, binary_to_bcd_converter_2_p4, binary_to_bcd_converter_2_p5
  Hex_Digit_Display hex_digit_display_8 (.value(binary_to_bcd_converter_2_p4));  // open: dp
  Hex_Digit_Display hex_digit_display_9 (.value(binary_to_bcd_converter_2_p3));  // open: dp
  Hex_Digit_Display hex_digit_display_10 (.value(binary_to_bcd_converter_2_p5));  // open: dp
  // Binary_to_BCD_converter #(.binvalue(13)) binary_to_bcd_converter_3: pin names not known
  _7447 #(.ShowInternalStructure("true")) u_7447_1 (
    .pin1(Digit[1]), .pin2(Digit[2]), .pin6(Digit[3]), .pin7(Digit[0]), .pin15(SE_F), .pin14(SE_G),
    .pin13(SE_A), .pin12(SE_B), .pin11(SE_C), .pin10(SE_D), .pin9(SE_E));  // open: pin3, pin4, pin5
  // Binary_to_BCD_converter #(.binvalue(7)) binary_to_bcd_converter_4: pin names not known
  // Binary_to_BCD_converter #(.binvalue(4)) binary_to_bcd_converter_5: pin names not known
  _7_Segment_Display u_7_segment_display_6 (
    .g(SE_G), .f(SE_F), .a(SE_A), .b(SE_B), .e(SE_E), .d(SE_D), .c(SE_C), .dp(in_24));

  // Other names for the same wires on the sheet: A = in_13; B = in_14; C = in_15; D = in_16; DEC = in_12;
  //   DEC_P = in_22; B_A = Digit[0]; B_B = Digit[1]; B_C = Digit[2]; B_D = Digit[3]; E = in_17; F = in_19; G = in_21;
  //   S_A = in_1; S_B = in_2; S_C = in_3; S_D = in_4; S_E = in_5; S_F = in_9; S_G = in_10

  // Notes on the sheet:
  //   Control of every
  //   single segment
  //   Decimal Point: Yes
  //   0 to 9
  //   Decimal Point: No
  //   Control of every
  //   single segment
  //   Decimal Point: Yes
  //   0 to F
  //   Decimal Point: Yes
  //   0 to 9
  //   Decimal Point: No
  //   0 to F
  //   Decimal Point: Yes
  //   0 to 8191
  //   Decimal Point: No
  //   0 to 8191
  //   Decimal Point: No
  //   Hex Digit Display
  //   Decimal Point
  //   Up to 6-bit
  //   Up to 10-bit
  //   Up to 13-bit
endmodule
