// Logisim project gates.circ as structural Verilog: 1 circuit, main circuit main
module main (
  input  in_1,
  input  in_2,
  input  in_3,
  input  in_4,
  input  in_5,
  input  in_6,
  input  in_7,
  input  in_8,
  input  in_9,
  input  in_10,
  input  in_11,
  input  in_12,
  input  in_13,
  input  in_14
);

  wire and_1_out, buffer_1_out, nand_1_out, nor_1_out, not_1_out, or_1_out, xnor_1_out, xor_1_out;

  not not_1 (not_1_out, in_1);
  buf buffer_1 (buffer_1_out, in_2);
  and and_1 (and_1_out, in_3, in_4);
  or or_1 (or_1_out, in_5, in_6);
  nand nand_1 (nand_1_out, in_7, in_8);
  nor nor_1 (nor_1_out, in_9, in_10);
  xor xor_1 (xor_1_out, in_11, in_12);
  xnor xnor_1 (xnor_1_out, in_13, in_14);
  // Probe on not_1_out
  // Probe on buffer_1_out
  // Probe on and_1_out
  // Probe on or_1_out
  // Probe on nand_1_out
  // Probe on nor_1_out
  // Probe on xor_1_out
  // Probe on xnor_1_out
endmodule
